// Logisim project Accensione_Spegnimento.circ as structural Verilog: 1 circuit, main circuit main
module main (
  input  Reset_temperatura,
  input  Alza_temperatura,
  input  CLK,
  input  ACCENSIONE,
  input  SPEGNIMENTO,
  output out_6,
  output out_7,
  output out_8,
  output out_9,
  output out_10,
  output out_11,
  output out_12,
  output out_13,
  output SEGNALE_ON
);

  wire main_1_p4;

  // Bottone_premuto_1bit_main main_1: pin names not known; wires that end beside it: CLK, ACCENSIONE, SPEGNIMENTO, main_1_p4
  // Shift_Register #(.length(10), .parallel("false")) shift_register_1: pin names not known; wires that end beside it: out_9, CLK, SPEGNIMENTO, out_8
  // Shift_Register #(.length(10), .parallel("false")) shift_register_2: pin names not known; wires that end beside it: out_10, CLK, SPEGNIMENTO, out_9, Alza_temperatura, Reset_temperatura, out_6
  // Shift_Register #(.length(10), .parallel("false")) shift_register_3: pin names not known; wires that end beside it: out_11, CLK, SPEGNIMENTO, out_10, Reset_temperatura, Alza_temperatura, out_6
  // Shift_Register #(.length(10), .parallel("false")) shift_register_4: pin names not known; wires that end beside it: out_12, CLK, SPEGNIMENTO, out_11
  // Shift_Register #(.length(10), .parallel("false")) shift_register_5: pin names not known; wires that end beside it: out_13, CLK, SPEGNIMENTO, out_12
  // Shift_Register #(.length(10), .parallel("false")) shift_register_6: pin names not known; wires that end beside it: main_1_p4, CLK, SPEGNIMENTO, out_13
  // Bottone_premuto_1bit_main main_2: pin names not known; wires that end beside it: CLK

  assign out_7 = out_6;
  assign SEGNALE_ON = out_8;
endmodule
